# Fritzing sketch Temperature (saved by Fritzing 0.9.3b)
circuit board: 8.46667cm x 5.64444cm
stripboards: 1

parts:
  Part1 = Arduino Nano (Rev3.0)
  R1 = Resistor [tolerance=±5% resistance=4.7k package=THT]
  0_91_Inch_I2C_OLED_Display1 = 0.91 Inch I2C OLED Display
  J1 = female pin header, 3 pins [form="♀ (female)"]

nets (from the schematic view):
  GND: Part1.GND, 0_91_Inch_I2C_OLED_Display1.GND, J1.pin3
  N1: Part1.A7, R1.Pin_0, J1.pin2
  N2: Part1.A5, 0_91_Inch_I2C_OLED_Display1.SCK
  N3: Part1.A4, 0_91_Inch_I2C_OLED_Display1.SDA
  3V3: Part1.3V3, R1.Pin_1, 0_91_Inch_I2C_OLED_Display1.VCC, J1.pin1

custom parts:
  0.91 Inch I2C OLED Display: Strong contrast by the use of the innovative OLED technology in the wide 0.91 inch Display! Due to the high resolution of 128x32 pixels the Display offers plenty of space to Display items! Easy connection of the display with Arduino, Raspberry Pi, and co. by I2C interface only four Pins! Thanks To The Standard Controller (SSD 1306) already libraries for Arduino, Raspberry Pi, and co. exist,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
